# Fritzing sketch Sketch2 (saved by Fritzing 0.9.8b)
breadboards: 1

parts:
  R1 = Resistor [tolerance=±5% power=0.25 resistance=10k package=THT]
  R2 = Resistor [tolerance=±5% power=0.25 resistance=100 package=THT]
  S1 = Pushbutton [package="[THT]"]
  J1 = Basic Force Sensing Resistor (FSR) [package=THT]
  J2 = Piezo Speaker
  Part1 = Arduino Uno (Rev3)

nets:
  N1: R1.Pin_0, R2.Pin_1, J2.pin1, Part1.GND
  N2: R1.Pin_1, J1.pin_0, Part1.A0
  N3: R2.Pin_0, S1.Pin_1, S1.Pin_2, Part1.D2
  N4: S1.Pin_3, S1.Pin_4, J1.pin_1, Part1.5V
  N5: J2.pin2, Part1.D9_PWM
