# Fritzing sketch Sketch_first_code (saved by Fritzing 0.9.8b)
breadboards: 1

parts:
  J1 = Piezo Speaker
  Part1 = Arduino Uno (Rev3)
  S1 = Pushbutton [package="[THT]"]
  R1 = Resistor [tolerance=±5% power=0.25 resistance=100 package=THT]
  HC-SR04_Sensor_1 = HC-SR04 Ultrasonic Distance Sensor

nets:
  N1: J1.pin1, Part1.GND
  N2: J1.pin2, Part1.D9_PWM
  N3: Part1.D8, HC-SR04_Sensor_1.TRIG
  N4: Part1.D2, S1.Pin_1, S1.Pin_2, R1.Pin_0
  N5: Part1.D7, HC-SR04_Sensor_1.ECHO
  5V: Part1.5V, S1.Pin_3, S1.Pin_4, HC-SR04_Sensor_1.VCC
  N6: R1.Pin_1, HC-SR04_Sensor_1.GND

// code stored in the sketch: Untitled2.ino

